# Fritzing sketch ElectronicsSubHArdware (saved by Fritzing 0.9.3b)
breadboards: 2

parts:
  Part1 = BME280 Breakout
  A1 = ESP32 DOIT DEVKIT V1 36pin
  Part4 = HX711 Weighing Sensor Module
  Load_Cell2 = Load Cell - Red/white/black/green  # not connected
  Load_Cell3 = Load Cell - Red/white/black/green
  Mod1 = Full Size SD Card Module
  ESP32_-_Back1 = ESP32 - CAM
  ZS-042_RTC1 = ZS-042 RTC Module
  OLED_I2C1 = OLED 128x64 I2C Monochrome Display
  U1 = LIPO-2000mAh [package=lipo-2000]
  R1 = PHOTOCELL [package=photocell-kit]
  R2 = Resistor [tolerance=±5% resistance=100 package=THT]
  Q1 = TRANSISTOR_NPN [package=to-92]
  R3 = Resistor [tolerance=±5% resistance=1k package=THT]
  R4 = Resistor [tolerance=±5% resistance=10k package=THT]

nets:
  N1: Part1.GND, U1.-, R1.P$2, Q1.E
  N2: Part1.3.3V, U1.+, R2.Pin_0, R3.Pin_0
  N3: Part1.SDI/SDA, Part1.SCK/SCL, A1.Pin_32, ZS-042_RTC1.SDA, OLED_I2C1.SDA
  N4: A1.Pin_7, Q1.C, R3.Pin_1
  N5: A1.Pin_10, Part4.DO/RX
  N6: A1.Pin_26, Part4.CK/TX
  N7: A1.Pin_27, ESP32_-_Back1.GPIO1_/_TX
  N8: A1.Pin_28, ESP32_-_Back1.GPIO3_/_RX
  N9: A1.Pin_29, Mod1.pin_7
  N10: A1.Pin_30, Mod1.pin_11
  N11: A1.Pin_31, Mod1.pin_13
  N12: A1.Pin_35, ZS-042_RTC1.SCL, OLED_I2C1.SCK
  N13: A1.Pin_36, Mod1.pin_9
  N14: Part4.B+, Load_Cell3.wire3
  N15: Part4.B-, Load_Cell3.wire4
  N16: R1.P$1, R2.Pin_1, R4.Pin_1
  N17: Q1.B, R4.Pin_0

custom parts:
  ESP32 DOIT DEVKIT V1 36pin: ESP32 DOIT DEVKIT V1 36pin.
  HX711 Weighing Sensor Module: HX711 is a precision 24-bit analog-to-digital converter (ADC) designed for weigh scales and industrial control applications to interface directly with a bridge sensor.
  Load Cell - Red/white/black/green: A rectangle load cell/weighting pressure Sensor with four wires - Red, white, black, green. Normally corresponding with E+, E-, A+, A- respectively.
  Full Size SD Card Module: SD Card Module Slot Socket Reader For Arduino ARM MCU
  ESP32 - CAM: The ESP32-CAM has a very competitive small-size camera module that can operate independently as a minimum system with a footprint of only 27*40.5*4.5mm and a deep sleep current of up to 6mA.
